# Fritzing sketch diagram (saved by Fritzing 0.9.4)
circuit board: 8.46667cm x 5.64444cm
breadboards: 1

parts:
  Part2 = Adafruit BME680 [part_number="Adafruit #3660"]
  Part1 = Adafruit Feather HUZZAH ESP8266 [part_number="Adafruit #2821"]
  Part3 = Adafruit 2.9" eInk Display Breakout [part_number="Adafruit #1028"]

nets:
  GND: Part2.GND, Part1.GND, Part3.GND
  VCC: Part2.VCC, Part1.3.3V, Part3.VIN
  N1: Part2.SCK/SCL, Part1.GPIO5/SCL
  N2: Part2.SDI/SDA, Part1.GPIO4/SDA
  N3: Part1.GPIO12/MISO, Part3.MISO
  N4: Part1.GPIO13/MOSI, Part3.MOSI
  N5: Part1.GPIO14/SCK, Part3.SCLK
  N6: Part1.RESET, Part3.RESET
  N7: Part1.GPIO15, Part3.DISPCS
  N8: Part1.GPIO16, Part3.SRAMCS
  N9: Part1.GPIO2, Part3.DC

custom parts:
  Adafruit Feather HUZZAH ESP8266: his is the Adafruit Feather HUZZAH ESP8266 - our take on an 'all-in-one' ESP8266 WiFi development board with built in USB and battery charging. Its an ESP8266 WiFi module with all the extras you need, ready to rock! We have other boards in the Feather family, check'em out here. At the Feather HUZZAH's heart is an ESP8266 WiFi microcontroller clocked at 80 MHz and at 3.3V logic. This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
  Adafruit 2.9" eInk Display Breakout: Easy e-paper finally comes to microcontrollers, with this breakout that's designed to make it a breeze to add a tri-color eInk display. Chances are you've seen one of those new-fangled 'e-readers' like the Kindle or Nook. They have gigantic electronic paper 'static' displays - that means the image stays on the display even when power is completely disconnected. The image is also high contrast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
